# Fritzing sketch esquematico (saved by Fritzing 0.9.0b)
breadboards: 1

parts:
  J1 = Infrared Proximity Sensor
  J2 = Infrared Proximity Sensor
  J3 = Basic Servo
  J4 = Basic Servo
  Circuito_Controlador = Arduino Uno (Rev3)
  S1 = Round Pushbutton
  LED1 = LED - 5mm [color="Red (633nm)" package="5 mm [THT]"]
  S2 = Square Pushbutton
  J5 = Piezo Speaker

nets:
  N1: J1.Vout, Circuito_Controlador.A0
  GND: J1.GND, J2.GND, J3.gnd, J4.gnd, Circuito_Controlador.GND, S1.leg0, LED1.anode, S2.leg1, J5.pin1
  VCC: J1.Vcc, J2.Vcc, J3.vcc, J4.vcc, Circuito_Controlador.VIN
  N2: J2.Vout, Circuito_Controlador.A1
  N3: J3.pulse, Circuito_Controlador.D6_PWM
  N4: J4.pulse, Circuito_Controlador.D5_PWM
  N5: Circuito_Controlador.D2, S1.leg1
  N6: Circuito_Controlador.D3_PWM, S2.leg0
  N7: Circuito_Controlador.D4, J5.pin2
  N8: Circuito_Controlador.D7, LED1.cathode
